// Logisim project basics.circ as structural Verilog
module main (
  input  [3:0] in_1,
  input  [3:0] in_2,
  output [4:0] out_3
);

  FOURbitsum fourbitsum_1 (.a(in_1), .b(in_2), .S(out_3));
  FOURbitsubtra fourbitsubtra_1 ();  // open: A, B, S
  Comp2s comp2s_1 ();  // open: A, B, S
  FourbitAdder_Sub fourbitadder_sub_1 ();  // open: A, B, in_3, out_4
  fourbitsumVHDL fourbitsumvhdl_1 (.A(in_1), .B(in_2));  // open: S
endmodule

module halfsum (
  input  a,
  input  b,
  output s,
  output cout
);

  xor xor_1 (s, a, b);
  and and_1 (cout, a, b);
endmodule

module sum (
  input  a,
  input  b,
  input  cin,
  output S,
  output cout
);

  wire halfsum_1_cout, halfsum_1_s, halfsum_2_cout;

  halfsum halfsum_1 (.a(a), .b(b), .s(halfsum_1_s), .cout(halfsum_1_cout));
  halfsum halfsum_2 (.a(cin), .b(halfsum_1_s), .s(S), .cout(halfsum_2_cout));
  or or_1 (cout, halfsum_2_cout, halfsum_1_cout);
endmodule

module FOURbitsum (
  input  [3:0] a,
  input  [3:0] b,
  output [4:0] S
);

  wire sum_1_cout, sum_2_cout, sum_3_cout;

  sum sum_1 (.a(a[0]), .b(b[0]), .cin(1'b0), .S(S[0]), .cout(sum_1_cout));
  sum sum_2 (.a(a[1]), .b(b[1]), .cin(sum_1_cout), .S(S[1]), .cout(sum_2_cout));
  sum sum_3 (.a(a[2]), .b(b[2]), .cin(sum_2_cout), .S(S[2]), .cout(sum_3_cout));
  sum sum_4 (.a(a[3]), .b(b[3]), .cin(sum_3_cout), .S(S[3]), .cout(S[4]));
endmodule

module halsub (
  input  a,
  input  b,
  output s,
  output Borrow
);

  wire not_1_out;

  xor xor_1 (s, a, b);
  not not_1 (not_1_out, a);
  and and_1 (Borrow, not_1_out, b);
endmodule

module sub (
  input  A,
  input  B,
  input  Bin,
  output s,
  output Bout
);

  wire halsub_1_borrow, halsub_1_s, halsub_2_borrow;

  halsub halsub_1 (.a(A), .b(B), .s(halsub_1_s), .Borrow(halsub_1_borrow));
  halsub halsub_2 (.a(halsub_1_s), .b(Bin), .s(s), .Borrow(halsub_2_borrow));
  or or_1 (Bout, halsub_2_borrow, halsub_1_borrow);
endmodule

module FOURbitsubtra (
  input  [3:0] A,
  input  [3:0] B,
  output [4:0] S
);

  wire sub_1_bout, sub_2_bout, sub_3_bout;

  sub sub_1 (.A(A[0]), .B(B[0]), .s(S[0]), .Bout(sub_1_bout));  // open: Bin
  sub sub_2 (.A(A[1]), .B(B[1]), .Bin(sub_1_bout), .s(S[1]), .Bout(sub_2_bout));
  sub sub_3 (.A(A[2]), .B(B[2]), .Bin(sub_2_bout), .s(S[2]), .Bout(sub_3_bout));
  sub sub_4 (.A(A[3]), .B(B[3]), .Bin(sub_3_bout), .s(S[3]), .Bout(S[4]));
endmodule

module Comp2s (
  input  [3:0] A,
  input  [3:0] B,
  output [4:0] S
);

  wire sum_1_cout, sum_2_cout, sum_3_cout, xor_1_out, xor_2_out, xor_3_out, xor_4_out;

  xor xor_1 (xor_1_out, B[0], 1'b1);
  xor xor_2 (xor_2_out, B[1], 1'b1);
  xor xor_3 (xor_3_out, B[2], 1'b1);
  xor xor_4 (xor_4_out, B[3], 1'b1);
  sum sum_1 (.a(A[0]), .b(xor_1_out), .cin(1'b1), .S(S[0]), .cout(sum_1_cout));
  sum sum_2 (.a(A[1]), .b(xor_2_out), .cin(sum_1_cout), .S(S[1]), .cout(sum_2_cout));
  sum sum_3 (.a(A[2]), .b(xor_3_out), .cin(sum_2_cout), .S(S[2]), .cout(sum_3_cout));
  sum sum_4 (.a(A[3]), .b(xor_4_out), .cin(sum_3_cout), .S(S[3]), .cout(S[4]));
endmodule

module Halfaddersub (
  input  A,
  input  B,
  input  chaveseletora,
  output S,
  output Cin_or_Bin
);

  wire xor_1_out;

  xor xor_1 (xor_1_out, A, chaveseletora);
  xor xor_2 (S, A, B);
  and and_1 (Cin_or_Bin, xor_1_out, B);
endmodule

module addersub (
  input  A,
  input  B,
  input  Cout_or_Bin,
  input  selec_key,
  output S,
  output Cout_or_Bout
);

  wire halfaddersub_1_cin_or_bin, halfaddersub_1_s, halfaddersub_2_cin_or_bin;

  Halfaddersub halfaddersub_1 (
    .A(A), .B(B), .chaveseletora(selec_key), .S(halfaddersub_1_s), .Cin_or_Bin(halfaddersub_1_cin_or_bin));
  Halfaddersub halfaddersub_2 (
    .A(halfaddersub_1_s), .B(Cout_or_Bin), .chaveseletora(selec_key), .S(S),
    .Cin_or_Bin(halfaddersub_2_cin_or_bin));
  or or_1 (Cout_or_Bout, halfaddersub_1_cin_or_bin, halfaddersub_2_cin_or_bin);
endmodule

module FourbitAdder_Sub (
  input  [3:0] A,
  input  [3:0] B,
  input  in_3,
  output [4:0] out_4
);

  wire addersub_1_cout_or_bout, addersub_2_cout_or_bout, addersub_3_cout_or_bout;

  addersub addersub_1 (
    .A(A[0]), .B(B[0]), .selec_key(in_3), .S(out_4[0]), .Cout_or_Bout(addersub_1_cout_or_bout));  // open: Cout_or_Bin
  addersub addersub_2 (
    .A(A[1]), .B(B[1]), .Cout_or_Bin(addersub_1_cout_or_bout), .selec_key(in_3), .S(out_4[1]),
    .Cout_or_Bout(addersub_2_cout_or_bout));
  addersub addersub_3 (
    .A(A[2]), .B(B[2]), .Cout_or_Bin(addersub_2_cout_or_bout), .selec_key(in_3), .S(out_4[2]),
    .Cout_or_Bout(addersub_3_cout_or_bout));
  addersub addersub_4 (
    .A(A[3]), .B(B[3]), .Cout_or_Bin(addersub_3_cout_or_bout), .selec_key(in_3), .S(out_4[3]),
    .Cout_or_Bout(out_4[4]));
endmodule

module fourbitsumVHDL (
  input  [3:0] A,
  input  [3:0] B,
  output [4:0] S
);

  wire vhdlsum_1_cout, vhdlsum_2_cout, vhdlsum_3_cout;

  vhdlsum vhdlsum_1 (.A(A[0]), .B(B[0]), .Cin(1'b0), .S(S[0]), .Cout(vhdlsum_1_cout));
  vhdlsum vhdlsum_2 (.A(A[1]), .B(B[1]), .Cin(vhdlsum_1_cout), .S(S[1]), .Cout(vhdlsum_2_cout));
  vhdlsum vhdlsum_3 (.A(A[2]), .B(B[2]), .Cin(vhdlsum_2_cout), .S(S[2]), .Cout(vhdlsum_3_cout));
  vhdlsum vhdlsum_4 (.A(A[3]), .B(B[3]), .Cin(vhdlsum_3_cout), .S(S[3]), .Cout(S[4]));
endmodule

module fourbitsubVHDL (
  input  [3:0] A,
  input  [3:0] B,
  output [4:0] S
);

  wire vhdlsub_1_bout, vhdlsub_2_bout, vhdlsub_3_bout;

  VHDLSUB vhdlsub_1 (.A(A[0]), .B(B[0]), .bin(1'b0), .S(S[0]), .bout(vhdlsub_1_bout));
  VHDLSUB vhdlsub_2 (.A(A[1]), .B(B[1]), .bin(vhdlsub_1_bout), .S(S[1]), .bout(vhdlsub_2_bout));
  VHDLSUB vhdlsub_3 (.A(A[2]), .B(B[2]), .bin(vhdlsub_2_bout), .S(S[2]), .bout(vhdlsub_3_bout));
  VHDLSUB vhdlsub_4 (.A(A[3]), .B(B[3]), .bin(vhdlsub_3_bout), .S(S[3]), .bout(S[4]));
endmodule

module Subde2VHDL (
  input  [3:0] A,
  input  [3:0] B,
  output [4:0] out_3
);

  wire sub2vhdl_1_cout, sub2vhdl_2_cout, sub2vhdl_3_cout;

  sub2VHdl sub2vhdl_1 (.A(A[0]), .B(B[0]), .Cin(1'b1), .S(out_3[0]), .Cout(sub2vhdl_1_cout));
  sub2VHdl sub2vhdl_2 (.A(A[1]), .B(B[1]), .Cin(sub2vhdl_1_cout), .S(out_3[1]), .Cout(sub2vhdl_2_cout));
  sub2VHdl sub2vhdl_3 (.A(A[2]), .B(B[2]), .Cin(sub2vhdl_2_cout), .S(out_3[2]), .Cout(sub2vhdl_3_cout));
  sub2VHdl sub2vhdl_4 (.A(A[3]), .B(B[3]), .Cin(sub2vhdl_3_cout), .S(out_3[3]), .Cout(out_3[4]));
endmodule

module addsubVHDL (
  input  [3:0] in_1,
  input  [3:0] in_2,
  input  in_3,
  output [4:0] out_4
);

  wire addsub_1_cbout, addsub_2_cbout, addsub_3_cbout;

  Addsub addsub_1 (.A(in_1[0]), .B(in_2[0]), .CBin(1'b0), .M(in_3), .S(out_4[0]), .CBout(addsub_1_cbout));
  Addsub addsub_2 (.A(in_1[1]), .B(in_2[1]), .CBin(addsub_1_cbout), .M(in_3), .S(out_4[1]), .CBout(addsub_2_cbout));
  Addsub addsub_3 (.A(in_1[2]), .B(in_2[2]), .CBin(addsub_2_cbout), .M(in_3), .S(out_4[2]), .CBout(addsub_3_cbout));
  Addsub addsub_4 (.A(in_1[3]), .B(in_2[3]), .CBin(addsub_3_cbout), .M(in_3), .S(out_4[3]), .CBout(out_4[4]));
endmodule

// VHDL entity vhdlsum, as the project stores it:
--------------------------------------------------------------------------------
-- Project :
-- File    :
-- Autor   :
-- Date    :
--
--------------------------------------------------------------------------------
-- Description :
--
--------------------------------------------------------------------------------

LIBRARY ieee;
USE ieee.std_logic_1164.all;

ENTITY vhdlsum IS
  PORT (
  ------------------------------------------------------------------------------
   A  :in  std_logic;
   B : in  std_logic;
   Cin : in  std_logic;

   S : out  std_logic;
   Cout : out std_logic
    );
END vhdlsum;

--------------------------------------------------------------------------------
--Complete your VHDL description below
--------------------------------------------------------------------------------

ARCHITECTURE TypeArchitecture OF vhdlsum IS

BEGIN
S<= ((A xor B)xor Cin);
Cout <= ((A and B) or ((A xor B) and Cin));

END TypeArchitecture;

// VHDL entity VHDLSUB, as the project stores it:
--------------------------------------------------------------------------------
-- Project :
-- File    :
-- Autor   :
-- Date    :
--
--------------------------------------------------------------------------------
-- Description :
--
--------------------------------------------------------------------------------

LIBRARY ieee;
USE ieee.std_logic_1164.all;

ENTITY VHDLSUB IS
  PORT (
  A : in std_logic;
  B : in std_logic;
  bin: in std_logic;

  S : out std_logic;
  bout : out std_logic
   
    );
END VHDLSUB;

--------------------------------------------------------------------------------
--Complete your VHDL description below
--------------------------------------------------------------------------------

ARCHITECTURE TypeArchitecture OF VHDLSUB IS

BEGIN
S <= ((A xor B)xor bin);
bout <= ((not A and B) or ( (not (A xor B)) and bin));

END TypeArchitecture;

// VHDL entity sub2VHdl, as the project stores it:
--------------------------------------------------------------------------------
-- Project :
-- File    :
-- Autor   :
-- Date    :
--
--------------------------------------------------------------------------------
-- Description :
--
--------------------------------------------------------------------------------

LIBRARY ieee;
USE ieee.std_logic_1164.all;

ENTITY sub2VHdl IS
  PORT (
  ------------------------------------------------------------------------------
   A  :in  std_logic;
   B : in  std_logic;
   Cin : in  std_logic;

   S : out  std_logic;
   Cout : out std_logic

    );
END sub2VHdl;

--------------------------------------------------------------------------------
--Complete your VHDL description below
--------------------------------------------------------------------------------

ARCHITECTURE TypeArchitecture OF sub2VHdl IS

BEGIN

S<= ((A xor not B)xor Cin);
Cout <= ((A and not B) or ((A xor not B) and Cin));


END TypeArchitecture;

// VHDL entity Addsub, as the project stores it:
--------------------------------------------------------------------------------
-- Project :
-- File    :
-- Autor   :
-- Date    :
--
--------------------------------------------------------------------------------
-- Description :
--
--------------------------------------------------------------------------------

LIBRARY ieee;
USE ieee.std_logic_1164.all;

ENTITY Addsub IS
  PORT (
  ------------------------------------------------------------------------------
   A  :in  std_logic;
   B : in  std_logic;
   CBin : in  std_logic;
   M : in std_logic;

   S : out  std_logic;
   CBout : out std_logic
    );
END Addsub;

--------------------------------------------------------------------------------
--Complete your VHDL description below
--------------------------------------------------------------------------------

ARCHITECTURE TypeArchitecture OF Addsub IS

BEGIN
S <= ((A xor B)xor CBin);
CBout <=((((A xor B)xor M) and CBin) or ((A xor M) and B));


END TypeArchitecture;
