// Logisim project display.circ as structural Verilog
module conversor (
  input  ov,
  input  s1,
  input  s0,
  output a,
  output b,
  output c,
  output d,
  output e,
  output f,
  output g
);

  wire and_1_out, and_2_out, and_3_out, and_4_out, and_5_out, and_6_out, and_7_out, and_8_out, and_9_out,
       and_10_out, and_11_out, and_12_out, and_13_out, and_14_out, and_15_out, and_16_out, and_17_out,
       not_1_out, not_2_out, not_3_out, or_1_out, or_2_out, or_3_out, or_6_out, or_7_out, or_10_out,
       or_11_out;

  not not_1 (not_1_out, ov);
  not not_2 (not_2_out, s1);
  not not_3 (not_3_out, s0);
  and and_1 (and_1_out, not_1_out, not_3_out);
  or or_1 (or_1_out, and_1_out, s1);
  and and_2 (and_2_out, ov, s0);
  or or_2 (or_2_out, not_1_out, and_3_out);
  and and_3 (and_3_out, not_2_out, not_3_out);
  and and_4 (and_4_out, s1, s0);
  or or_3 (or_3_out, not_2_out, s0);
  or or_4 (c, or_3_out, ov);
  and and_5 (and_5_out, not_1_out, not_3_out);
  and and_6 (and_6_out, not_1_out, s1);
  and and_7 (and_7_out, ov, not_2_out);
  and and_8 (and_8_out, and_7_out, s0);
  and and_9 (and_9_out, s1, not_3_out);
  and and_10 (and_10_out, not_1_out, not_3_out);
  or or_5 (e, and_10_out, and_11_out);
  and and_11 (and_11_out, s1, not_3_out);
  and and_12 (and_12_out, not_2_out, not_3_out);
  or or_6 (or_6_out, and_12_out, and_13_out);
  and and_13 (and_13_out, ov, not_2_out);
  and and_14 (and_14_out, ov, not_3_out);
  and and_15 (and_15_out, not_1_out, s1);
  or or_7 (or_7_out, and_15_out, and_16_out);
  and and_16 (and_16_out, ov, not_2_out);
  and and_17 (and_17_out, s1, not_3_out);
  or or_8 (a, or_1_out, and_2_out);
  or or_9 (b, or_2_out, and_4_out);
  or or_10 (or_10_out, and_5_out, and_6_out);
  or or_11 (or_11_out, and_8_out, and_9_out);
  or or_12 (f, or_6_out, and_14_out);
  or or_13 (g, or_7_out, and_17_out);
  or or_14 (d, or_10_out, or_11_out);
endmodule

module convSIMP (
  input  s0,
  input  s1,
  input  ov,
  output a,
  output b,
  output c,
  output d,
  output e,
  output f,
  output g
);

  wire and_2_out, and_3_out, and_4_out, and_5_out, and_6_out, not_1_out, not_2_out, not_3_out, not_4_out,
       not_5_out, not_6_out, not_7_out, not_8_out, not_9_out, not_10_out, not_11_out, or_1_out, or_2_out,
       or_5_out, or_7_out, xor_1_out, xor_2_out, xor_3_out;

  not not_1 (not_1_out, ov);
  not not_2 (not_2_out, s0);
  or or_1 (or_1_out, not_1_out, s1);
  and and_1 (e, not_2_out, or_1_out);
  not not_3 (not_3_out, s1);
  not not_4 (not_4_out, s0);
  xor xor_1 (xor_1_out, ov, s0);
  not not_5 (not_5_out, ov);
  and and_2 (and_2_out, not_5_out, s1);
  not not_6 (not_6_out, s1);
  and and_3 (and_3_out, ov, not_6_out, s0);
  and and_4 (and_4_out, not_3_out, not_4_out);
  or or_2 (or_2_out, not_3_out, not_4_out);
  xor xor_2 (xor_2_out, ov, s1);
  not not_7 (not_7_out, s0);
  not not_8 (not_8_out, xor_1_out);
  xor xor_3 (xor_3_out, s1, s0);
  not not_9 (not_9_out, xor_3_out);
  not not_10 (not_10_out, ov);
  not not_11 (not_11_out, s1);
  and and_5 (and_5_out, ov, or_2_out);
  and and_6 (and_6_out, not_7_out, s1);
  or or_3 (a, not_8_out, s1);
  or or_4 (b, not_9_out, not_10_out);
  or or_5 (or_5_out, not_11_out, ov);
  or or_6 (c, or_5_out, s0);
  or or_7 (or_7_out, and_2_out, and_3_out);
  or or_8 (d, or_7_out, e);
  or or_9 (f, and_4_out, and_5_out);
  or or_10 (g, xor_2_out, and_6_out);

  // Other names for the same wires on the sheet: tx = ov; ty = s1; tz = s0
endmodule

module teste (
  input  x,
  input  y,
  input  z,
  output c,
  output r
);

  wire and_1_out, and_2_out, not_1_out, not_2_out, or_1_out;

  not not_1 (not_1_out, x);
  not not_2 (not_2_out, z);
  and and_1 (and_1_out, not_1_out, not_2_out);
  and and_2 (and_2_out, y, not_2_out);
  or or_1 (or_1_out, not_1_out, y);
  and and_3 (r, or_1_out, not_2_out);
  or or_2 (c, and_1_out, and_2_out);
endmodule

module ttt (
  input  [3:0] in_1
);

  wire [6:0] decodificador_hex_vhdl_1_saida;

  decodificador_hex_vhdl decodificador_hex_vhdl_1 (.saida(decodificador_hex_vhdl_1_saida));  // open: entrada
  _7_Segment_Display u_7_segment_display_1 (
    .g(decodificador_hex_vhdl_1_saida[0]), .f(decodificador_hex_vhdl_1_saida[1]),
    .a(decodificador_hex_vhdl_1_saida[6]), .b(decodificador_hex_vhdl_1_saida[5]),
    .e(decodificador_hex_vhdl_1_saida[2]), .d(decodificador_hex_vhdl_1_saida[3]),
    .c(decodificador_hex_vhdl_1_saida[4]));  // open: dp
endmodule

// VHDL entity decodificador_hex_vhdl, as the project stores it:
library IEEE;
use IEEE.STD_LOGIC_1164.ALL;

entity decodificador_hex_vhdl is
    Port (
        entrada : in  STD_LOGIC_VECTOR(3 downto 0);
        saida   : out STD_LOGIC_VECTOR(6 downto 0)
    );
end decodificador_hex_vhdl;

architecture Behavioral of decodificador_hex_vhdl is
begin
    process(entrada)
    begin
        case entrada is
            when "0000" => saida <= "1111110";
            when "0001" => saida <= "0110000";
            when "0010" => saida <= "1101101";
            when "0011" => saida <= "1111001";
            when "0100" => saida <= "0110011";
            when "0101" => saida <= "1011011";
            when "0110" => saida <= "1011111";
            when "0111" => saida <= "1110000";
            when "1000" => saida <= "1111111";
            when "1001" => saida <= "1111011";
            when "1010" => saida <= "1110111";
            when "1011" => saida <= "0011111";
            when "1100" => saida <= "1001110";
            when "1101" => saida <= "0111101";
            when "1110" => saida <= "1001111";
            when "1111" => saida <= "1000111";
            when others => saida <= "0000000";
        end case;
    end process;
end Behavioral;
