// Logisim project flipsnoflops.circ as structural Verilog
module flipflobrs (
  input  set,
  input  reset,
  output q,
  output nq
);

  nand nand_1 (q, ~set, nq);  // NAND_Gate
  nand nand_2 (nq, q, ~reset);  // NAND_Gate
endmodule

module flipflopRScoc (
  input  in_1,
  input  in_2,
  output out_3,
  output out_4
);

  wire clock_1_out, nand_1_out, nand_2_out;

  Clock clock_1 (.out(clock_1_out));
  nand nand_1 (nand_1_out, in_1, clock_1_out);
  nand nand_2 (nand_2_out, clock_1_out, in_2);
  flipflobrs flipflobrs_1 (.set(nand_1_out), .reset(nand_2_out), .q(out_3), .nq(out_4));
endmodule

module JK_GAL (
  input  preset,
  input  j,
  input  cock,
  input  k,
  input  clear,
  output q,
  output Nq
);

  wire nand_1_out, nand_2_out;

  nand nand_1 (nand_1_out, j, cock, Nq);
  nand nand_2 (nand_2_out, q, cock, k);
  nand nand_3 (q, preset, nand_1_out, Nq);
  nand nand_4 (Nq, q, nand_2_out, clear);
endmodule

module Jk_ME_PC (
  input  PS,
  input  j,
  input  clock,
  input  k,
  input  CLR,
  output q,
  output nq
);

  wire nand_1_out, nand_2_out, nand_3_out, nand_4_out, nand_5_out, nand_6_out, not_1_out, not_2_out,
       not_3_out;

  not not_1 (not_1_out, PS);
  nand nand_1 (nand_1_out, j, clock, nq);
  nand nand_2 (nand_2_out, q, clock, k);
  not not_2 (not_2_out, CLR);
  nand nand_3 (nand_3_out, not_1_out, nand_1_out, nand_4_out);
  nand nand_4 (nand_4_out, nand_3_out, nand_2_out, not_2_out);
  not not_3 (not_3_out, clock);
  nand nand_5 (nand_5_out, nand_3_out, not_3_out);
  nand nand_6 (nand_6_out, nand_4_out, not_3_out);
  nand nand_7 (q, not_1_out, nand_5_out, nq);
  nand nand_8 (nq, q, nand_6_out, not_2_out);
endmodule

module JK_ME_PC_T (
  input  PS,
  input  T,
  input  clock,
  input  CLR,
  output q,
  output nq
);

  wire nand_1_out, nand_2_out, nand_3_out, nand_4_out, nand_5_out, nand_6_out, not_1_out, not_2_out,
       not_3_out;

  not not_1 (not_1_out, PS);
  nand nand_1 (nand_1_out, T, clock, nq);
  nand nand_2 (nand_2_out, q, clock, T);
  not not_2 (not_2_out, CLR);
  nand nand_3 (nand_3_out, not_1_out, nand_1_out, nand_4_out);
  nand nand_4 (nand_4_out, nand_3_out, nand_2_out, not_2_out);
  not not_3 (not_3_out, clock);
  nand nand_5 (nand_5_out, nand_3_out, not_3_out);
  nand nand_6 (nand_6_out, nand_4_out, not_3_out);
  nand nand_7 (q, not_1_out, nand_5_out, nq);
  nand nand_8 (nq, q, nand_6_out, not_2_out);
endmodule

module JK_ME_PC_D (
  input  preset,
  input  D,
  input  clock,
  input  clear,
  output q,
  output nq
);

  wire nand_1_out, nand_2_out, nand_3_out, nand_4_out, nand_5_out, nand_6_out, not_1_out, not_2_out,
       not_3_out, not_4_out;

  not not_1 (not_1_out, D);
  nand nand_1 (nand_1_out, D, clock, nq);
  nand nand_2 (nand_2_out, q, clock, not_1_out);
  not not_2 (not_2_out, preset);
  nand nand_3 (nand_3_out, not_2_out, nand_1_out, nand_4_out);
  nand nand_4 (nand_4_out, nand_3_out, nand_2_out, not_3_out);
  not not_3 (not_3_out, clear);
  not not_4 (not_4_out, clock);
  nand nand_5 (nand_5_out, nand_3_out, not_4_out);
  nand nand_6 (nand_6_out, nand_4_out, not_4_out);
  nand nand_7 (q, not_2_out, nand_5_out, nq);
  nand nand_8 (nq, q, nand_6_out, not_3_out);
endmodule

module shifter_reg (
  input  in_1,
  input  sel,
  input  par1,
  input  par2,
  input  serie,
  input  cock,
  output s1,
  output s0
);

  wire button_1_out, button_2_out, conversor_1_a, conversor_1_b, conversor_1_c, conversor_1_d, conversor_1_e,
       conversor_1_f, conversor_1_g, mux2_1_ot, mux2_2_ot;

  Button button_1 (.out(button_1_out));
  // JK_ME_PC_T jk_me_pc_t_1: pin names not known
  MUX2 mux2_1 (.x(sel), .s1(par1), .s2(serie), .ot(mux2_1_ot));
  Button button_2 (.out(button_2_out));
  JK_ME_PC_D jk_me_pc_d_1 (
    .preset(button_1_out), .D(mux2_1_ot), .clock(cock), .clear(button_2_out), .q(s1));  // open: nq
  MUX2 mux2_2 (.x(sel), .s1(par2), .s2(s1), .ot(mux2_2_ot));
  JK_ME_PC_D jk_me_pc_d_2 (
    .preset(button_1_out), .D(mux2_2_ot), .clock(cock), .clear(button_2_out), .q(s0));  // open: nq
  conversor conversor_1 (
    .ov(in_1), .s1(s1), .s0(s0), .a(conversor_1_a), .b(conversor_1_b), .c(conversor_1_c), .d(conversor_1_d),
    .e(conversor_1_e), .f(conversor_1_f), .g(conversor_1_g));
  _7_Segment_Display u_7_segment_display_1 (
    .g(conversor_1_g), .f(conversor_1_f), .a(conversor_1_a), .b(conversor_1_b), .e(conversor_1_e),
    .d(conversor_1_d), .c(conversor_1_c));  // open: dp
endmodule

module DIVfrenq (
  input  preset,
  input  t,
  input  clock,
  input  clear,
  output out_5,
  output out_6,
  output out_7,
  output out_8
);

  Jk_ME_PC jk_me_pc_1 (.PS(preset), .j(t), .clock(clock), .k(t), .CLR(clear), .q(out_5));  // open: nq
  Jk_ME_PC jk_me_pc_2 (.PS(preset), .j(t), .clock(out_5), .k(t), .CLR(clear), .q(out_6));  // open: nq
  Jk_ME_PC jk_me_pc_3 (.PS(preset), .j(t), .clock(out_6), .k(t), .CLR(clear), .q(out_7));  // open: nq
  Jk_ME_PC jk_me_pc_4 (.PS(preset), .j(t), .clock(out_7), .k(t), .CLR(clear), .q(out_8));  // open: nq
  Hex_Digit_Display hex_digit_display_1 (.value({out_8, out_7, out_6, out_5}));  // open: dp
endmodule

module divcon (
  input  in_1,
  input  preset,
  input  t,
  input  cock,
  input  clear,
  output out_6,
  output out_7
);

  wire conversor_1_a, conversor_1_b, conversor_1_c, conversor_1_d, conversor_1_e, conversor_1_f,
       conversor_1_g;

  Jk_ME_PC jk_me_pc_1 (.PS(preset), .j(t), .clock(cock), .k(t), .CLR(clear), .q(out_6));  // open: nq
  Jk_ME_PC jk_me_pc_2 (.PS(preset), .j(t), .clock(out_6), .k(t), .CLR(clear), .q(out_7));  // open: nq
  conversor conversor_1 (
    .ov(in_1), .s1(out_7), .s0(out_6), .a(conversor_1_a), .b(conversor_1_b), .c(conversor_1_c),
    .d(conversor_1_d), .e(conversor_1_e), .f(conversor_1_f), .g(conversor_1_g));
  _7_Segment_Display u_7_segment_display_1 (
    .g(conversor_1_g), .f(conversor_1_f), .a(conversor_1_a), .b(conversor_1_b), .e(conversor_1_e),
    .d(conversor_1_d), .c(conversor_1_c));  // open: dp
endmodule

module MUX2 (
  input  x,
  input  s1,
  input  s2,
  output ot
);

  wire and_1_out, and_2_out, not_1_out;

  not not_1 (not_1_out, x);
  and and_1 (and_1_out, not_1_out, s1);
  and and_2 (and_2_out, x, s2);
  or or_1 (ot, and_1_out, and_2_out);
endmodule

module MUX4 (
  input  y1,
  input  y2,
  input  y3,
  input  y4,
  input  [1:0] sel,
  output s
);

  wire and_1_out, and_2_out, and_3_out, and_4_out, not_1_out, not_2_out, not_3_out, not_4_out, or_1_out,
       or_2_out;

  not not_1 (not_1_out, sel[0]);
  and and_1 (and_1_out, y1, not_1_out, not_2_out);
  not not_2 (not_2_out, sel[1]);
  not not_3 (not_3_out, sel[1]);
  and and_2 (and_2_out, y2, not_3_out, sel[0]);
  and and_3 (and_3_out, y3, sel[1], not_4_out);
  not not_4 (not_4_out, sel[0]);
  and and_4 (and_4_out, y4, sel[1], sel[0]);
  or or_1 (or_1_out, and_1_out, and_2_out);
  or or_2 (or_2_out, and_3_out, and_4_out);
  or or_3 (s, or_1_out, or_2_out);
endmodule

module shifterUNI (
  input  [1:0] PRL,
  input  SE,
  input  SD,
  input  ck,
  input  [1:0] sel,
  output out_6,
  output out_7
);

  wire clr_out, mux4_1_s, mux4_2_s, ps_out;

  MUX4 mux4_1 (.y1(out_6), .y2(out_7), .y3(SD), .y4(PRL[1]), .sel(sel), .s(mux4_1_s));
  Button clr (.out(clr_out));
  Button ps (.out(ps_out));
  JK_ME_PC_D jk_me_pc_d_1 (.preset(ps_out), .D(mux4_1_s), .clock(ck), .clear(clr_out), .q(out_6));  // open: nq
  MUX4 mux4_2 (.y1(out_7), .y2(SE), .y3(out_6), .y4(PRL[0]), .sel(sel), .s(mux4_2_s));
  JK_ME_PC_D jk_me_pc_d_2 (.preset(ps_out), .D(mux4_2_s), .clock(ck), .clear(clr_out), .q(out_7));  // open: nq
endmodule
