// Logisim project Esquematum.circ as structural Verilog: 6 circuits, main circuit main
module main (
);

  seletor seletor_1 ();  // open: entrada, s1, s2, s3, s4, s5, s6, s7, s8
  SUMandENABLE sumandenable_1 ();  // open: A, B, enable, s
endmodule

module seletor (
  input  [2:0] entrada,
  output s1,
  output s2,
  output s3,
  output s4,
  output s5,
  output s6,
  output s7,
  output s8
);

  wire and_1_out, and_2_out, and_3_out, and_4_out, and_5_out, and_6_out, and_7_out, and_8_out, not_1_out,
       not_2_out, not_3_out;

  not not_1 (not_1_out, entrada[2]);
  not not_2 (not_2_out, entrada[1]);
  not not_3 (not_3_out, entrada[0]);
  and and_1 (and_1_out, not_1_out, not_2_out);
  and and_2 (and_2_out, not_1_out, not_2_out);
  and and_3 (and_3_out, not_1_out, entrada[1]);
  and and_4 (and_4_out, not_1_out, entrada[1]);
  and and_5 (and_5_out, entrada[2], not_2_out);
  and and_6 (and_6_out, entrada[2], not_2_out);
  and and_7 (and_7_out, entrada[2], entrada[1]);
  and and_8 (and_8_out, entrada[2], entrada[1]);
  and and_9 (s1, and_1_out, not_3_out);
  and and_10 (s2, and_2_out, entrada[0]);
  and and_11 (s3, and_3_out, not_3_out);
  and and_12 (s4, and_4_out, entrada[0]);
  and and_13 (s5, and_5_out, not_3_out);
  and and_14 (s6, and_6_out, entrada[0]);
  and and_15 (s7, and_7_out, not_3_out);
  and and_16 (s8, and_8_out, entrada[0]);
endmodule

module enable2bits (
  input  ent1,
  input  ent2,
  input  enable,
  output s1,
  output s2
);

  and and_1 (s1, ent1, enable);
  and and_2 (s2, ent2, enable);
endmodule

module meiosomador (
  input  A,
  input  B,
  output S,
  output OV
);

  xor xor_1 (S, A, B);
  and and_1 (OV, A, B);
endmodule

module somador2bits (
  input  [1:0] A,
  input  CIN,
  input  [1:0] B,
  output [2:0] out_4
);

  wire meiosomador_1_ov, meiosomador_1_s, meiosomador_2_ov, meiosomador_2_s, meiosomador_3_ov,
       meiosomador_4_ov, or_1_out;

  meiosomador meiosomador_1 (.A(A[0]), .B(CIN), .S(meiosomador_1_s), .OV(meiosomador_1_ov));
  meiosomador meiosomador_2 (.A(A[1]), .B(or_1_out), .S(meiosomador_2_s), .OV(meiosomador_2_ov));
  or or_1 (or_1_out, meiosomador_3_ov, meiosomador_1_ov);
  or or_2 (out_4[2], meiosomador_4_ov, meiosomador_2_ov);
  meiosomador meiosomador_3 (.A(meiosomador_1_s), .B(B[0]), .S(out_4[0]), .OV(meiosomador_3_ov));
  meiosomador meiosomador_4 (.A(meiosomador_2_s), .B(B[1]), .S(out_4[1]), .OV(meiosomador_4_ov));
endmodule

module SUMandENABLE (
  input  [1:0] A,
  input  [1:0] B,
  input  enable,
  output [2:0] s
);

  wire [1:0] enable2bits_1_s1, enable2bits_2_s1;

  enable2bits enable2bits_1 (
    .ent1(A[0]), .ent2(A[1]), .enable(enable), .s1(enable2bits_1_s1[0]), .s2(enable2bits_1_s1[1]));
  enable2bits enable2bits_2 (
    .ent1(B[0]), .ent2(B[1]), .enable(enable), .s1(enable2bits_2_s1[0]), .s2(enable2bits_2_s1[1]));
  somador2bits somador2bits_1 (.A(enable2bits_1_s1), .CIN(1'b0), .B(enable2bits_2_s1), .out_4(s));
endmodule
