// Logisim project demux.circ as structural Verilog: 4 circuits, main circuit main
module main (
);

  demux8 demux8_1 ();  // open: A, key, y1, y2, y3, y4, y5, y6, y7, y8
endmodule

module demux2 (
  input  [3:0] A,
  input  chave,
  output [3:0] y1,
  output [3:0] y2
);

  wire [3:0] not_1_out;

  assign not_1_out = ~{4{chave}};  // NOT_Gate not_1, 4 bits wide
  assign y1 = A & not_1_out;  // AND_Gate and_1, 4 bits wide
  assign y2 = A & {4{chave}};  // AND_Gate and_2, 4 bits wide
endmodule

module demux4 (
  input  [3:0] A,
  input  [1:0] key,
  output [3:0] y1,
  output [3:0] y2,
  output [3:0] y3,
  output [3:0] y4
);

  wire [3:0] demux2_1_y1, demux2_1_y2;

  demux2 demux2_1 (.A(A), .chave(key[1]), .y1(demux2_1_y1), .y2(demux2_1_y2));
  demux2 demux2_2 (.A(demux2_1_y1), .chave(key[0]), .y1(y1), .y2(y2));
  demux2 demux2_3 (.A(demux2_1_y2), .chave(key[0]), .y1(y3), .y2(y4));
endmodule

module demux8 (
  input  [3:0] A,
  input  [2:0] key,
  output [3:0] y1,
  output [3:0] y2,
  output [3:0] y3,
  output [3:0] y4,
  output [3:0] y5,
  output [3:0] y6,
  output [3:0] y7,
  output [3:0] y8
);

  wire [3:0] demux2_1_y1, demux2_1_y2;

  demux2 demux2_1 (.A(A), .chave(key[2]), .y1(demux2_1_y1), .y2(demux2_1_y2));
  demux4 demux4_1 (.A(demux2_1_y1), .key(key[1:0]), .y1(y1), .y2(y2), .y3(y3), .y4(y4));
  demux4 demux4_2 (.A(demux2_1_y2), .key(key[1:0]), .y1(y5), .y2(y6), .y3(y7), .y4(y8));
endmodule
