// Logisim project meioaddsubparaothinkcad.circ as structural Verilog: 3 circuits, main circuit main
module main (
  input  a,
  input  b,
  input  s1,
  input  s2,
  input  a1,
  input  b1,
  output [2:0] out_7
);

  wire and_1_out, and_2_out, and_3_out, and_4_out, qwyfgwd_1_o, teste_1_m, teste_1_s;

  teste teste_1 (.a(s1), .b(s2), .s(teste_1_s), .m(teste_1_m));
  and and_1 (and_1_out, a, teste_1_s);
  and and_2 (and_2_out, b, teste_1_s);
  and and_3 (and_3_out, a1, teste_1_s);
  and and_4 (and_4_out, b1, teste_1_s);
  qwyfgwd qwyfgwd_1 (.a(and_1_out), .c(1'b0), .b(and_2_out), .m(teste_1_m), .s(out_7[0]), .o(qwyfgwd_1_o));
  qwyfgwd qwyfgwd_2 (.a(and_3_out), .c(qwyfgwd_1_o), .b(and_4_out), .m(teste_1_m), .s(out_7[1]), .o(out_7[2]));
endmodule

module qwyfgwd (
  input  a,
  input  c,
  input  b,
  input  m,
  output s,
  output o
);

  wire and_1_out, and_2_out, xor_1_out, xor_2_out, xor_3_out;

  xor xor_1 (xor_1_out, a, m);
  xor xor_2 (xor_2_out, a, c);
  and and_1 (and_1_out, xor_1_out, c);
  xor xor_3 (xor_3_out, xor_2_out, m);
  and and_2 (and_2_out, xor_3_out, b);
  or or_1 (o, and_2_out, and_1_out);
  xor xor_4 (s, xor_2_out, b);
endmodule

module teste (
  input  a,
  input  b,
  output s,
  output m
);

  wire and_1_out, and_2_out, not_1_out, not_2_out;

  not not_1 (not_1_out, a);
  not not_2 (not_2_out, b);
  and and_1 (and_1_out, not_1_out, b);
  and and_2 (and_2_out, a, not_2_out);
  and and_3 (m, not_1_out, b);
  or or_1 (s, and_1_out, and_2_out);
endmodule
