// Logisim project trabalhofinalinconpleto.circ as structural Verilog
module sum (
  input  esc,
  input  a,
  input  cin,
  input  b,
  output s,
  output Cout,
  output Sesc
);

  wire and_1_out, and_2_out, and_3_out, and_4_out, and_5_out, and_6_out, and_7_out, not_1_out, not_2_out,
       not_3_out;

  not not_1 (not_1_out, a);
  not not_2 (not_2_out, cin);
  not not_3 (not_3_out, b);
  and and_1 (and_1_out, esc, not_1_out, not_2_out, b);
  and and_2 (and_2_out, esc, not_1_out, cin, not_3_out);
  and and_3 (and_3_out, esc, a, not_2_out, not_3_out);
  and and_4 (and_4_out, esc, a, cin, b);
  and and_5 (and_5_out, esc, cin, b);
  and and_6 (and_6_out, esc, a, b);
  and and_7 (and_7_out, esc, a, cin);
  or or_1 (s, and_1_out, and_2_out, and_3_out, and_4_out);
  or or_2 (Cout, and_5_out, and_6_out, and_7_out);

  assign Sesc = esc;
endmodule

module sub2 (
  input  [3:0] A,
  input  esc,
  input  [3:0] B,
  output [3:0] S,
  output Oinrrelevante
);

  wire sum_1_cout, sum_1_sesc, sum_2_cout, sum_2_sesc, sum_3_cout, sum_3_sesc, xor_1_out, xor_2_out,
       xor_3_out, xor_4_out;

  xor xor_1 (xor_1_out, B[0], 1'b1);
  xor xor_2 (xor_2_out, B[1], 1'b1);
  xor xor_3 (xor_3_out, B[2], 1'b1);
  xor xor_4 (xor_4_out, B[3], 1'b1);
  sum sum_1 (.esc(esc), .a(A[0]), .cin(1'b1), .b(xor_1_out), .s(S[0]), .Cout(sum_1_cout), .Sesc(sum_1_sesc));
  sum sum_2 (
    .esc(sum_1_sesc), .a(A[1]), .cin(sum_1_cout), .b(xor_2_out), .s(S[1]), .Cout(sum_2_cout),
    .Sesc(sum_2_sesc));
  sum sum_3 (
    .esc(sum_2_sesc), .a(A[2]), .cin(sum_2_cout), .b(xor_3_out), .s(S[2]), .Cout(sum_3_cout),
    .Sesc(sum_3_sesc));
  sum sum_4 (
    .esc(sum_3_sesc), .a(A[3]), .cin(sum_3_cout), .b(xor_4_out), .s(S[3]), .Cout(Oinrrelevante));  // open: Sesc
endmodule

module codificadorPrioridade (
  input  esc,
  input  [3:0] a,
  output [3:0] s
);

  wire and_2_out, and_3_out, and_4_out, and_5_out, and_8_out, and_9_out, not_1_out, not_2_out, not_3_out;

  not not_1 (not_1_out, a[3]);
  not not_2 (not_2_out, a[2]);
  not not_3 (not_3_out, a[1]);
  and and_1 (s[3], esc, a[3]);
  and and_2 (and_2_out, esc, not_1_out);
  and and_3 (and_3_out, esc, not_1_out);
  and and_4 (and_4_out, not_2_out, a[1]);
  and and_5 (and_5_out, esc, not_1_out);
  and and_6 (s[2], and_2_out, a[2]);
  and and_7 (s[1], and_3_out, and_4_out);
  and and_8 (and_8_out, and_5_out, not_2_out);
  and and_9 (and_9_out, not_3_out, a[0]);
  and and_10 (s[0], and_8_out, and_9_out);
endmodule

module comparadordemagntudi (
  input  a,
  input  b,
  output [1:0] s
);

  wire not_1_out, not_2_out;

  not not_1 (not_1_out, a);
  not not_2 (not_2_out, b);
  and and_1 (s[1], a, not_2_out);
  and and_2 (s[0], not_1_out, b);
endmodule

module detectordeZero (
  input  [3:0] A,
  input  esc,
  output out_3
);

  wire and_1_out, and_2_out, and_3_out, not_1_out, not_2_out, not_3_out, not_4_out;

  not not_1 (not_1_out, A[0]);
  not not_2 (not_2_out, A[1]);
  not not_3 (not_3_out, A[2]);
  not not_4 (not_4_out, A[3]);
  and and_1 (and_1_out, not_1_out, not_2_out);
  and and_2 (and_2_out, not_3_out, not_4_out);
  and and_3 (and_3_out, and_1_out, and_2_out);
  and and_4 (out_3, and_3_out, esc);
endmodule

module mux2 (
  input  [4:0] A,
  input  [4:0] B,
  input  SEL,
  output [4:0] S
);

  wire [4:0] and_1_out, and_2_out, not_1_out;

  assign not_1_out = ~{5{SEL}};  // NOT_Gate not_1, 5 bits wide
  assign and_1_out = B & {5{SEL}};  // AND_Gate and_1, 5 bits wide
  assign and_2_out = not_1_out & A;  // AND_Gate and_2, 5 bits wide
  assign S = and_2_out | and_1_out;  // OR_Gate or_1, 5 bits wide
endmodule

module mux4 (
  input  [4:0] D1,
  input  [4:0] D2,
  input  [4:0] D3,
  input  [4:0] D4,
  input  [1:0] SEL,
  output [4:0] S
);

  wire [4:0] mux2_1_s, mux2_2_s;

  mux2 mux2_1 (.A(D1), .B(D3), .SEL(SEL[1]), .S(mux2_1_s));
  mux2 mux2_2 (.A(D2), .B(D4), .SEL(SEL[1]), .S(mux2_2_s));
  mux2 mux2_3 (.A(mux2_1_s), .B(mux2_2_s), .SEL(SEL[0]), .S(S));
endmodule

module MUX8 (
  input  [4:0] D1,
  input  [4:0] D2,
  input  [4:0] D3,
  input  [4:0] D4,
  input  [4:0] D5,
  input  [4:0] D6,
  input  [4:0] D7,
  input  [4:0] D8,
  input  [2:0] CHAVE_SEL,
  output [4:0] S
);

  wire [4:0] mux4_1_s, mux4_2_s;

  mux4 mux4_1 (.D1(D1), .D2(D3), .D3(D5), .D4(D7), .SEL(CHAVE_SEL[2:1]), .S(mux4_1_s));
  mux4 mux4_2 (.D1(D2), .D2(D4), .D3(D6), .D4(D8), .SEL(CHAVE_SEL[2:1]), .S(mux4_2_s));
  mux2 mux2_1 (.A(mux4_1_s), .B(mux4_2_s), .SEL(CHAVE_SEL[0]), .S(S));
endmodule

module SUBmux (
  input  a,
  input  b,
  input  bin,
  output s,
  output c
);

  wire and_1_out, and_2_out, and_3_out, and_4_out, and_5_out, and_6_out, and_7_out, not_1_out, not_2_out,
       not_3_out;

  not not_1 (not_1_out, a);
  not not_2 (not_2_out, b);
  not not_3 (not_3_out, bin);
  and and_1 (and_1_out, not_1_out, not_2_out, bin);
  and and_2 (and_2_out, not_1_out, b, not_3_out);
  and and_3 (and_3_out, a, not_2_out, not_3_out);
  and and_4 (and_4_out, a, b, bin);
  and and_5 (and_5_out, not_1_out, bin);
  and and_6 (and_6_out, not_1_out, b);
  and and_7 (and_7_out, b, bin);
  or or_1 (s, and_1_out, and_2_out, and_3_out, and_4_out);
  or or_2 (c, and_5_out, and_6_out, and_7_out);
endmodule

module FULLSUBMAX (
  input  [3:0] A,
  input  [3:0] B,
  output [4:0] out_3
);

  wire submux_1_c, submux_2_c, submux_3_c;

  SUBmux submux_1 (.a(A[0]), .b(B[0]), .s(out_3[0]), .c(submux_1_c));  // open: bin
  SUBmux submux_2 (.a(A[1]), .b(B[1]), .bin(submux_1_c), .s(out_3[1]), .c(submux_2_c));
  SUBmux submux_3 (.a(A[2]), .b(B[2]), .bin(submux_2_c), .s(out_3[2]), .c(submux_3_c));
  SUBmux submux_4 (.a(A[3]), .b(B[3]), .bin(submux_3_c), .s(out_3[3]), .c(out_3[4]));
endmodule

module mainteste (
  input  [3:0] A,
  input  [3:0] B,
  input  [2:0] Chave,
  output [4:0] saida
);

  wire [4:0] dectde0mux_1_s, fullsubmax_1_out_3, fullsum_1_out_3, logic_andmux_1_s, or_logicmux_1_s,
       priorimux_1_s, sub2smux_1_out_3;

  fullsum fullsum_1 (.A(A), .B(B), .out_3(fullsum_1_out_3));
  FULLSUBMAX fullsubmax_1 (.A(A), .B(B), .out_3(fullsubmax_1_out_3));
  sub2sMUX sub2smux_1 (.B(B), .A(A), .out_3(sub2smux_1_out_3));
  logic_andmux logic_andmux_1 (.A(A), .B(B), .S(logic_andmux_1_s));
  OR_LOGICMUX or_logicmux_1 (.A(A), .B(B), .S(or_logicmux_1_s));
  PrioriMUX priorimux_1 (.a(A), .s(priorimux_1_s));
  dectDe0mux dectde0mux_1 (.a(A), .s(dectde0mux_1_s));
  MUX8 mux8_1 (
    .D1(fullsum_1_out_3), .D2(fullsubmax_1_out_3), .D3(sub2smux_1_out_3), .D4(logic_andmux_1_s),
    .D5(or_logicmux_1_s), .D6(priorimux_1_s), .D8(dectde0mux_1_s), .CHAVE_SEL(Chave), .S(saida));  // open: D7
endmodule

module MUXsum (
  input  a,
  input  b,
  input  cin,
  output s,
  output cout
);

  wire and_1_out, and_2_out, and_3_out, and_4_out, and_5_out, and_6_out, and_7_out, not_1_out, not_2_out,
       not_3_out;

  not not_1 (not_1_out, a);
  not not_2 (not_2_out, b);
  not not_3 (not_3_out, cin);
  and and_1 (and_1_out, not_1_out, not_2_out, cin);
  and and_2 (and_2_out, not_1_out, b, not_3_out);
  and and_3 (and_3_out, a, not_2_out, not_3_out);
  and and_4 (and_4_out, a, b, cin);
  and and_5 (and_5_out, b, cin);
  and and_6 (and_6_out, a, cin);
  and and_7 (and_7_out, a, b);
  or or_1 (s, and_1_out, and_2_out, and_3_out, and_4_out);
  or or_2 (cout, and_5_out, and_6_out, and_7_out);
endmodule

module fullsum (
  input  [3:0] A,
  input  [3:0] B,
  output [4:0] out_3
);

  wire muxsum_1_cout, muxsum_2_cout, muxsum_3_cout;

  MUXsum muxsum_1 (.a(A[0]), .b(B[0]), .s(out_3[0]), .cout(muxsum_1_cout));  // open: cin
  MUXsum muxsum_2 (.a(A[1]), .b(B[1]), .cin(muxsum_1_cout), .s(out_3[1]), .cout(muxsum_2_cout));
  MUXsum muxsum_3 (.a(A[2]), .b(B[2]), .cin(muxsum_2_cout), .s(out_3[2]), .cout(muxsum_3_cout));
  MUXsum muxsum_4 (.a(A[3]), .b(B[3]), .cin(muxsum_3_cout), .s(out_3[3]), .cout(out_3[4]));
endmodule

module sub2sMUX (
  input  [3:0] B,
  input  [3:0] A,
  output [4:0] out_3
);

  wire muxsum_1_cout, muxsum_2_cout, muxsum_3_cout, xor_1_out, xor_2_out, xor_3_out, xor_4_out;

  xor xor_1 (xor_1_out, B[0], 1'b1);
  xor xor_2 (xor_2_out, B[1], 1'b1);
  xor xor_3 (xor_3_out, B[2], 1'b1);
  xor xor_4 (xor_4_out, B[3], 1'b1);
  MUXsum muxsum_1 (.a(A[0]), .b(xor_1_out), .cin(1'b1), .s(out_3[0]), .cout(muxsum_1_cout));
  MUXsum muxsum_2 (.a(A[1]), .b(xor_2_out), .cin(muxsum_1_cout), .s(out_3[1]), .cout(muxsum_2_cout));
  MUXsum muxsum_3 (.a(A[2]), .b(xor_3_out), .cin(muxsum_2_cout), .s(out_3[2]), .cout(muxsum_3_cout));
  MUXsum muxsum_4 (.a(A[3]), .b(xor_4_out), .cin(muxsum_3_cout), .s(out_3[3]), .cout(out_3[4]));
endmodule

module logic_andmux (
  input  [3:0] A,
  input  [3:0] B,
  output [4:0] S
);

  and and_1 (S[0], A[0], B[0]);
  and and_2 (S[1], A[1], B[1]);
  and and_3 (S[2], A[2], B[2]);
  and and_4 (S[3], A[3], B[3]);

  assign S[4] = 1'b0;
endmodule

module OR_LOGICMUX (
  input  [3:0] A,
  input  [3:0] B,
  output [4:0] S
);

  or or_1 (S[0], A[0], B[0]);
  or or_2 (S[1], A[1], B[1]);
  or or_3 (S[2], A[2], B[2]);
  or or_4 (S[3], A[3], B[3]);

  assign S[4] = 1'b0;
endmodule

module PrioriMUX (
  input  [3:0] a,
  output [4:0] s
);

  wire not_1_out, not_2_out, not_3_out;

  not not_1 (not_1_out, a[3]);
  not not_2 (not_2_out, a[2]);
  not not_3 (not_3_out, a[1]);
  and and_1 (s[2], not_1_out, a[2]);
  and and_2 (s[1], not_1_out, not_2_out, a[1]);
  and and_3 (s[0], not_1_out, not_2_out, not_3_out, a[0]);

  assign s[4:3] = {1'b0, a[3]};
endmodule

module dectDe0mux (
  input  [3:0] a,
  output [4:0] s
);

  wire not_1_out, not_2_out, not_3_out, not_4_out;

  not not_1 (not_1_out, a[3]);
  not not_2 (not_2_out, a[2]);
  not not_3 (not_3_out, a[1]);
  not not_4 (not_4_out, a[0]);
  and and_1 (s[0], not_1_out, not_2_out, not_3_out, not_4_out);

  assign s[4:1] = 4'b0000;
endmodule
